# Fritzing sketch FritzingRotary (saved by Fritzing 0.9.3b)

parts:
  Part1 = Arduino Uno (Rev3)
  RE1 = Rotary Encoder [package=THT]

nets:
  N1: Part1.D2, RE1.EncoderPinB
  N2: Part1.D3_PWM, RE1.EncoderPinC
  N3: Part1.GND, RE1.EncoderPinA
